// Logisim project gglu_v2.circ as structural Verilog: 1 circuit, main circuit main
module main (
  input  Clk,
  input  D,
  input  i1,
  input  i0,
  input  in_5,
  output Dbus,
  output RR,
  output W,
  output J
);

  wire and_1_out, multiplexer_2_out, nor_1_out, nor_2_out, nor_3_out, not_1_out, not_3_out, not_4_out,
       undriven;

  Multiplexer multiplexer_1 (.in0(D), .in1(RR), .out(Dbus), .sel(i1));
  not not_1 (not_1_out, i1);
  // NOT_Gate not_2 has open pins: in=i1, out=open
  nor nor_1 (nor_1_out, Dbus, RR);
  nor nor_2 (nor_2_out, D, not_1_out);
  nor nor_3 (nor_3_out, i1, undriven);
  Multiplexer multiplexer_2 (.in0(Dbus), .in1(nor_1_out), .out(multiplexer_2_out), .sel(i0));
  nor nor_4 (in_5, nor_2_out, nor_3_out);
  and and_1 (and_1_out, Clk, not_3_out);
  not not_3 (not_3_out, i1);
  not not_4 (not_4_out, i0);
  // NOR_Gate nor_5 has open pins: in0=in_5, in1=undriven, out=open
  D_Flip_Flop d_ff_1 (.D(multiplexer_2_out), .clk(and_1_out), .Q(RR));  // open: Qn, preset, reset
  and and_2 (W, i1, Clk, not_4_out);
  and and_3 (J, i1, Clk, i0, nor_1_out);

  // Other names for the same wires on the sheet: Clock = Clk; Data = D
endmodule
